# Fritzing sketch montage (saved by Fritzing 0.9.0b)
breadboards: 1

parts:
  LED1 = LED - 5mm [color="Red (633nm)" package="5 mm [THT]"]
  LED2 = LED - 5mm [color="Red (633nm)" package="5 mm [THT]"]
  LED3 = LED - 5mm [color="Red (633nm)" package="5 mm [THT]"]
  LED4 = LED - 5mm [color="Red (633nm)" package="5 mm [THT]"]
  R1 = Resistor [tolerance=±5% resistance=220 package=THT]
  R2 = Resistor [tolerance=±5% resistance=220 package=THT]
  R3 = Resistor [tolerance=±5% resistance=220 package=THT]
  R4 = Resistor [tolerance=±5% resistance=220 package=THT]
  Composant1 = Arduino Mega 2560 (Rev3)  # not connected

nets:
  N1: LED1.cathode, R1.Pin_0
  N2: LED2.cathode, R2.Pin_0
  N3: LED3.cathode, R3.Pin_0
  N4: LED4.cathode, R4.Pin_0

notes:
  Pin 1 input
